# Fritzing sketch robot_cart-on (saved by Fritzing 0.9.3b)
breadboards: 2

parts:
  M1 = DC Motor
  M2 = DC Motor
  M3 = DC Motor
  M4 = DC Motor
  J1 = Basic Servo
  J2 = Basic Servo
  U1 = TCM8240MD [package=tcm8240md]  # not connected
  Grove1 = Grove OLED 128x96
  Grove2 = Grove OLED 128x96
  SP1 = SPEAKER [package=pcb_mount_speaker]
  MIC1 = Microphone
  IC1 = L293D [package=THT]
  IC2 = L293D [package=THT]
  Raspberry_Pi_2 = Raspberry Pi 4 [part_number=RPI-4-b]
  A1 = tf-luna lidar
  VCC1 = Battery block 9V
  LCD1 = TFT 3.5 inch 480x320 w touch and SD

nets:
  N1: M1.pin_1, IC1.Out_2_(_Controlled_by_Enable_1_)
  N2: M1.pin_2, IC1.Out_1_(_Controlled_by_Enable_1_)
  N3: M2.pin_1, IC2.Out_2_(_Controlled_by_Enable_1_)
  N4: M2.pin_2, IC2.Out_1_(_Controlled_by_Enable_1_)
  N5: M3.pin_1, IC1.Out_4_(_Controlled_by_Enable_2_)
  N6: M3.pin_2, IC1.Out_3_(_Controlled_by_Enable_2_)
  N7: M4.pin_1, IC2.Out_3_(_Controlled_by_Enable_2_)
  N8: M4.pin_2, IC2.Out_4_(_Controlled_by_Enable_2_)
  GND: J1.gnd, J1.pulse, J2.gnd, Grove1.GND, Grove2.GND, SP1.-, MIC1.pin1, IC1.0V, IC2.In_2, IC2.In_3, Raspberry_Pi_2.GND, Raspberry_Pi_2.GPIO22, Raspberry_Pi_2.ID_SD, Raspberry_Pi_2.GPIO13, Raspberry_Pi_2.GPIO20, Raspberry_Pi_2.GPIO7, A1.Pin_4, VCC1.-, LCD1.Pin_2
  VCC: J1.vcc, J2.vcc, SP1.+, Raspberry_Pi_2.5V, A1.Pin_1, LCD1.Pin_1, LCD1.Pin_8
  N9: J2.pulse, Raspberry_Pi_2.GPIO19
  VCC_2: Grove1.VCC, Grove2.VCC, MIC1.pin2, IC1.In_2, IC1.+V, Raspberry_Pi_2.3v3, Raspberry_Pi_2.3V3, Raspberry_Pi_2.GPIO23
  N10: Grove1.SDA, Grove2.SDA, Raspberry_Pi_2.GPIO2
  N11: Grove1.SCL, Grove2.SCL, Raspberry_Pi_2.GPIO3
  N12: IC1.Enable_1, Raspberry_Pi_2.GPIO17, Raspberry_Pi_2.GPIO18, LCD1.Pin_5
  N13: IC1.In_1, IC2.Enable_1, Raspberry_Pi_2.GPIO6, Raspberry_Pi_2.GPIO12
  N14: IC1.Enable_2, VCC1.+
  N15: IC1.In_3, Raspberry_Pi_2.GPIO5
  N16: IC1.In_4, Raspberry_Pi_2.GPIO27
  N17: IC2.In_1, Raspberry_Pi_2.GPIO26
  N18: IC2.In_4, Raspberry_Pi_2.GPIO21
  N19: IC2.+V, Raspberry_Pi_2.GPIO16
  N20: Raspberry_Pi_2.GPIO4, LCD1.Pin_4
  N21: Raspberry_Pi_2.GPIO10, LCD1.Pin_6, LCD1.Pin_12
  N22: Raspberry_Pi_2.GPIO9, LCD1.Pin_9, LCD1.Pin_13
  N23: Raspberry_Pi_2.GPIO11, LCD1.Pin_7, LCD1.Pin_10
  N24: Raspberry_Pi_2.GPIO8, LCD1.Pin_14
  N25: Raspberry_Pi_2.GPIO25, LCD1.Pin_11
  N26: Raspberry_Pi_2.GPIO24, LCD1.Pin_3
  N27: Raspberry_Pi_2.GPIO15, A1.Pin_3
  N28: Raspberry_Pi_2.GPIO14, A1.Pin_2

custom parts:
  Raspberry Pi 4: The RPi4, a faster version of the awesome Raspberry Pi 2 B ARM Board with 40 pin gpio. Ready for special Raspberry Pi B+ and RPi2 Hat (Hardware attached (on) top)
  tf-luna lidar: TF-Luna is using Time of Flight (TOF) principle to measure distance, and it periodically emits near infrared modulated wave.
  TFT 3.5 inch 480x320 w touch and SD: This is a generic 1.8 tft spi lcd display available on ebay and others. The 1.8"3.5 inch 480X320 SPI TFT Module 320x480 LCD Display - Touch.

// code stored in the sketch: notas.ino
//Pin 1: EN1 -> activa motor pin 12/13/18/19
//Pin2: IN1 -> dir A
//Pin3: Out1 -> cable motot
//Pin4, Pin5: GND
//Pin6: Out2 -> cable motor
//Pin7: In2 -> dir B
//Pin8: VMOT -> alimentació (6V)
